// Logisim project Circuit4.circ as structural Verilog: 1 circuit, main circuit main
module main (
  input  A,
  input  B,
  input  C,
  input  D,
  output Output
);

  wire and_1_out, and_2_out, nand_1_out, not_1_out, not_2_out, or_1_out, xor_1_out;

  not not_1 (not_1_out, D);
  not not_2 (not_2_out, A);
  and and_1 (and_1_out, B, C);
  xor xor_1 (xor_1_out, C, A);
  or or_1 (or_1_out, and_1_out, xor_1_out);
  and and_2 (and_2_out, not_2_out, D);
  nand nand_1 (nand_1_out, or_1_out, not_1_out);
  nor nor_1 (Output, and_2_out, nand_1_out);
endmodule
