// Logisim project Circuit5.circ as structural Verilog: 1 circuit, main circuit main
module main (
  input  in_1,
  input  in_2,
  input  in_3,
  output out_4
);

  wire and_1_out, nand_1_out;

  nand nand_1 (nand_1_out, in_1, in_2);
  and and_1 (and_1_out, in_2, in_3);
  or or_1 (out_4, nand_1_out, and_1_out);
endmodule
